# Fritzing sketch piezo-tune-player-circuit-v2.0 (saved by Fritzing 0.9.6b)
breadboards: 1

parts:
  Teensy_3_1 = Teensy 3.2  # not connected
  J1 = Piezo Speaker
  R1 = Resistor [tolerance=±5% power=0.25 resistance=10k package=THT]
  7_Segment1 = 7 Segment Display
  U1 = 74HC595 [package="DIP16 [THT]"]
  R2 = Resistor [tolerance=±5% resistance=220 package="0805 [SMD]"]
  R3 = Resistor [tolerance=±5% resistance=220 package="0805 [SMD]"]
  R4 = Resistor [tolerance=±5% resistance=220 package="0805 [SMD]"]
  R5 = Resistor [tolerance=±5% resistance=220 package="0805 [SMD]"]
  R6 = Resistor [tolerance=±5% resistance=220 package="0805 [SMD]"]
  R7 = Resistor [tolerance=±5% resistance=220 package="0805 [SMD]"]
  R8 = Resistor [tolerance=±5% resistance=220 package="0805 [SMD]"]
  R9 = Resistor [tolerance=±5% resistance=220 package="0805 [SMD]"]
  S1 = Momentary Switch [package=ksa_sealed_tac_switch]
  R10 = Resistor [tolerance=±5% resistance=220 package="0805 [SMD]"]

nets:
  N1: J1.pin1, U1.GND, U1.OE, R10.Pin_1
  N2: J1.pin2, R1.Pin_0
  N3: 7_Segment1.Segment_E, R6.Pin_0
  N4: 7_Segment1.Segment_D, R5.Pin_0
  N5: 7_Segment1.common_anode, U1.MR, U1.VCC, S1.4
  N6: 7_Segment1.Segment_C, R4.Pin_0
  N7: 7_Segment1.Segment_DP, R9.Pin_0
  N8: 7_Segment1.Segment_B, R3.Pin_0
  N9: 7_Segment1.Segment_A, R2.Pin_0
  N10: 7_Segment1.Segment_F, R7.Pin_0
  N11: 7_Segment1.Segment_G, R8.Pin_0
  N12: U1.Q1, R3.Pin_1
  N13: U1.Q2, R4.Pin_1
  N14: U1.Q3, R5.Pin_1
  N15: U1.Q4, R6.Pin_1
  N16: U1.Q5, R7.Pin_1
  N17: U1.Q6, R8.Pin_1
  N18: U1.Q7, R9.Pin_1
  N19: U1.Q0, R2.Pin_1
  N20: S1.1, R10.Pin_0

custom parts:
  Teensy 3.2: The Teensy is a complete USB-based microcontoller development system, in a very small footprint, capable of implementing many types of projects. All programming is done via the USB port. No special programmer is needed, only a standard micro-USB cable and a PC or Macintosh with a USB port. It has a USB keyboard/mouse/joystick emulation stack and can be programmed through Arduino IDE.
