# Fritzing sketch piezo-tune-player-circuit (saved by Fritzing 0.9.6b)
breadboards: 1

parts:
  Teensy_3_1 = Teensy 3.2  # not connected
  J1 = Piezo Speaker
  R1 = Resistor [tolerance=±5% power=0.25 resistance=10k package=THT]

nets:
  N1: J1.pin2, R1.Pin_0

custom parts:
  Teensy 3.2: The Teensy is a complete USB-based microcontoller development system, in a very small footprint, capable of implementing many types of projects. All programming is done via the USB port. No special programmer is needed, only a standard micro-USB cable and a PC or Macintosh with a USB port. It has a USB keyboard/mouse/joystick emulation stack and can be programmed through Arduino IDE.
